// Digital circuit 8-bit-ripple-carry-adder.dig as structural Verilog
module _8_bit_ripple_carry_adder (
  input  a,
  input  b,
  input  cin,
  output sum,
  output cout
);

  Add add_1 (.a(a), .b(b), .c_i(cin), .s(sum), .c_o(cout));
endmodule
