// Digital circuit max2.dig as structural Verilog
module max2 (
  input  [1:0] a0,
  input  [1:0] b0,
  input  [1:0] a1,
  input  [1:0] b1,
  output [1:0] r0,
  output [1:0] r1
);

  wire [1:0] and_1_out, and_2_out;

  assign and_1_out = a0 & b0;  // And and_1, 2 bits wide
  assign and_2_out = a1 & b1;  // And and_2, 2 bits wide
  assign r0 = and_1_out & and_2_out;  // And and_3, 2 bits wide

  assign r1 = r0;
endmodule
